// Logisim project 2pr1.circ as structural Verilog: 1 circuit, main circuit main
module main (
  input  A,
  input  B
);

  wire and_1_out, xor_1_out;

  xor xor_1 (xor_1_out, A, B);
  and and_1 (and_1_out, B, A);
  LED SUM (.in(xor_1_out));
  LED CARRY (.in(and_1_out));
endmodule
