// Logisim project 2pr3.circ as structural Verilog: 1 circuit, main circuit main
module main (
  input  l0,
  input  l1,
  input  S
);

  wire and_1_out, and_2_out, not_1_out, or_1_out;

  not not_1 (not_1_out, S);
  and and_1 (and_1_out, l0, l1);
  and and_2 (and_2_out, l0, not_1_out);
  or or_1 (or_1_out, and_1_out, and_2_out);
  LED y (.in(or_1_out));
endmodule
