// Logisim project 2pr4.circ as structural Verilog: 1 circuit, main circuit main
module main (
  input  A,
  input  B
);

  wire and_1_out, and_2_out, not_1_out, or_1_out;

  not not_1 (not_1_out, A);
  and and_1 (and_1_out, not_1_out, B);
  and and_2 (and_2_out, B, A);
  or or_1 (or_1_out, and_1_out, and_2_out);
  LED F (.in(or_1_out));
endmodule
