// Logisim project 3.2.circ as structural Verilog: 1 circuit, main circuit main
module main (
  input  D0,
  input  D1
);

  wire clock_1_out, d_ff_1_q, d_ff_2_q;

  Clock clock_1 (.out(clock_1_out));
  D_Flip_Flop d_ff_1 (.D(D0), .clk(clock_1_out), .Q(d_ff_1_q));  // open: Qn, preset, reset
  D_Flip_Flop d_ff_2 (.D(D1), .clk(clock_1_out), .Q(d_ff_2_q));  // open: Qn, preset, reset
  LED Q0 (.in(d_ff_1_q));
  LED Q1 (.in(d_ff_2_q));
endmodule
