// Logisim project 3.3.circ as structural Verilog: 1 circuit, main circuit main
module main (
  input  A,
  input  B
);

  wire and_1_out, and_2_out, and_3_out, clock_1_out, d_ff_1_q, not_1_out, xor_1_out;

  not not_1 (not_1_out, A);
  and and_1 (and_1_out, not_1_out, B);
  and and_2 (and_2_out, A, B);
  Clock clock_1 (.out(clock_1_out));
  xor xor_1 (xor_1_out, and_1_out, and_2_out);
  D_Flip_Flop d_ff_1 (.D(xor_1_out), .clk(clock_1_out), .Q(d_ff_1_q));  // open: Qn, preset, reset
  LED led_1 (.in(d_ff_1_q));
  and and_3 (and_3_out, clock_1_out, clock_1_out);
  LED S2 (.in(and_3_out));

  // Notes on the sheet:
  //   A&!Q
  //   A&Q
  //   D
  //   Q(S0/S1)
  //   Q&A
endmodule
